// Logisim project mips.circ as structural Verilog: 11 circuits, main circuit MIPS32
module MIPS32 (
  input  power,
  input  reset
);

  wire clk_out, e_m_1_out_11, execute_1_we, hazard_1_a, hazard_1_ac, hazard_1_b, hazard_1_bc, m_w_1_out_11,
       memory_1_weo, not_1_out;
  wire [4:0] d_e_1_out_14, d_e_1_out_15, d_e_1_out_18, d_e_1_out_19, decode_1_rd, decode_1_rs, decode_1_rt,
       decode_1_shamt, e_m_1_out_10, execute_1_rdo, m_w_1_out_10, memory_1_rdo;
  wire [11:0] d_e_1_out_16, decode_1_fcn;
  wire [31:0] d_e_1_out_12, d_e_1_out_13, d_e_1_out_17, decode_1_a, decode_1_b, decode_1_imm, e_m_1_out_8,
       e_m_1_out_9, execute_1_bfwd, execute_1_d, m_w_1_out_8, memory_1_do, memory_1_m, mipsprogramrom_1_p2,
       multiplexer_1_out, multiplexer_2_out, multiplexer_3_out, multiplexer_4_out, pc_1_pc, register_1_q;

  Clock clk (.out(clk_out));
  pc pc_1 (.clk(clk_out), .en(power), .pc(pc_1_pc));
  // MIPSProgramROM mipsprogramrom_1: pin names not known; wires that end beside it: pc_1_pc, mipsprogramrom_1_p2
  Register #(.width(32)) register_1 (.D(mipsprogramrom_1_p2), .en(power), .clk(clk_out), .Q(register_1_q), .clr(reset));
  decode decode_1 (
    .W(m_w_1_out_8), .clk(clk_out), .wE(m_w_1_out_11), .rW(m_w_1_out_10), .Inst(register_1_q),
    .A(decode_1_a), .B(decode_1_b), .rd(decode_1_rd), .shamt(decode_1_shamt), .fcn(decode_1_fcn),
    .imm(decode_1_imm), .rs(decode_1_rs), .rt(decode_1_rt));
  Multiplexer #(.width(32), .enable("false")) multiplexer_1 (
    .in0(e_m_1_out_8), .in1(m_w_1_out_8), .out(multiplexer_1_out), .sel(hazard_1_bc));
  d_e d_e_1 (
    .fcn(decode_1_fcn), .out_13(d_e_1_out_13), .out_14(d_e_1_out_14), .A(decode_1_a), .shamt(decode_1_shamt),
    .out_12(d_e_1_out_12), .imm(decode_1_imm), .out_15(d_e_1_out_15), .en(power), .rd(decode_1_rd),
    .B(decode_1_b), .out_16(d_e_1_out_16), .clk(clk_out), .out_17(d_e_1_out_17), .res(reset),
    .rs(decode_1_rs), .rt(decode_1_rt), .out_18(d_e_1_out_18), .out_19(d_e_1_out_19));
  Multiplexer #(.width(32), .enable("false")) multiplexer_2 (
    .in0(d_e_1_out_12), .in1(multiplexer_3_out), .out(multiplexer_2_out), .sel(hazard_1_a));
  Multiplexer #(.width(32), .enable("false")) multiplexer_3 (
    .in0(e_m_1_out_8), .in1(m_w_1_out_8), .out(multiplexer_3_out), .sel(hazard_1_ac));
  Multiplexer #(.width(32), .enable("false")) multiplexer_4 (
    .in0(multiplexer_1_out), .in1(d_e_1_out_13), .out(multiplexer_4_out), .sel(not_1_out));
  not not_1 (not_1_out, hazard_1_b);
  execute execute_1 (
    .A(multiplexer_2_out), .B(multiplexer_4_out), .rd(d_e_1_out_14), .shamt(d_e_1_out_15),
    .fcn(d_e_1_out_16), .imm(d_e_1_out_17), .D(execute_1_d), .Bfwd(execute_1_bfwd), .rdo(execute_1_rdo),
    .we(execute_1_we));
  e_m e_m_1 (
    .clk(clk_out), .we(execute_1_we), .B(execute_1_bfwd), .out_9(e_m_1_out_9), .D(execute_1_d),
    .rd(execute_1_rdo), .out_8(e_m_1_out_8), .out_10(e_m_1_out_10), .out_11(e_m_1_out_11), .en(power),
    .r(reset));
  hazard hazard_1 (
    .emRW(e_m_1_out_11), .emRD(e_m_1_out_10), .ieRS(d_e_1_out_18), .ieRT(d_e_1_out_19), .mwRW(m_w_1_out_11),
    .mwRD(m_w_1_out_10), .a(hazard_1_a), .b(hazard_1_b), .ac(hazard_1_ac), .bc(hazard_1_bc));
  memory memory_1 (
    .D(e_m_1_out_8), .B(e_m_1_out_9), .rd(e_m_1_out_10), .we(e_m_1_out_11), .Do(memory_1_do), .M(memory_1_m),
    .rdo(memory_1_rdo), .weo(memory_1_weo));
  m_w m_w_1 (
    .out_8(m_w_1_out_8), .rd(memory_1_rdo), .D(memory_1_do), .clk(clk_out), .en(power), .M(memory_1_m),
    .we(memory_1_weo), .out_10(m_w_1_out_10), .out_11(m_w_1_out_11), .res(reset));  // open: out_9

  // Notes on the sheet:
  //   contents of mipsprogramrom_1 (hex, n*v repeats v):
  //   #addiu tests addiu $1, $0, 3248 #0x00000cb0 addiu $2, $0, 803  #0x00000323  #The following
  //   instructions are not yet supported by this Mini-MIPS32 processor. Thus, they should not change any
  //   values of registers or jump to any new PC address. The remaining instructions should proceed as
  //   normal. # BEQ $1, $1, -20 # BEQ $1, $1, 4  # BNE $1, $1, 28304 # BNE $2, $1, -10032  # BLEZ $1, 8028
  //   # BLEZ $3, -280 # BLEZ $0, 20364  # BGTZ $1, 39488 # BGTZ $3, 80 # BGTZ $0, 8232  # BLTZ $1, -2392 #
  //   BLTZ $3, 23928 # BLTZ $0, 1804  # BGEZ $1, 9204 # BGEZ $3, 20 # BGEZ $0, -3812  # J 1897340 # J 2904
  //   # JR $2 # JR $3 # JAL 8232 # JAL 22020 # JALR $2 # JALR $3  # SW $1, 2012($1) # SB $2, 10324($1) #
  //   LW $2, 4804($1) # LB $3, -2392($3) # LBU $1, 280($1) #end of unsupported instructions, the following
  //   should proceed normally.  subu $3, $2, $1 #0xfffff673 addu $4, $1, $3 #0x00000323  #andi tests andi
  //   $5, $2, 779 #0x00000303  #ori tests ori $6, $1, 3490 #0x00000db2  #xori tests xori $7, $1, 20239
  //   #0x000043bf  #slti slti $8, $1, -3292 #0x00000000 slti $9, $1, 32500 #0x00000001  #sltiu sltiu $10,
  //   $1, 20   #0x00000000 sltiu $11, $1, 4309 #0x00000001  #and and $12, $1, $2 #0x00000020  #or or $13,
  //   $1, $2 #00000fb3  #xor xor $14, $1, $3 #0xfffff04c  #nor nor $15, $1, $2 #0xfffff04c  #slt slt $16,
  //   $1, $17 #0x00000000 slt $17, $3, $1 #0x00000001  #sltu sltu $18, $1, $2 #0x00000000 sltu $19, $2, $1
  //   #0x00000001  #movn movn $20, $1, $2 #0x00000cb0 movn $21, $1, $0 #0x00000000  #movz movz $22, $2, $2
  //   #0x00000000 movz $23, $2, $0 #0x00000323  #sll sll $24, $1, 23 #58000000  #srl srl $25, $2, 5
  //   #0x00000019 srl $26, $3, 9 #0x007ffffb  #sra sra $27, $2, 13 #0x00000000  #sllv sllv $28, $1, $2
  //   #0x00006580  #srlv srlv $29, $3, $1 #0x0000ffff  #srav srav $30, $3, $2 #0xfffffece  #lui lui $31,
  //   2803 #0x0af30000  #The following instructions test possible hazards that require forwarding logic,
  //   both individually as well as combinations of errors. Nops separate the instructions in each set to
  //   isolate the dependencies:  #1a. EX/MEM.RegisterRd == ID/EX.RegisterRs addiu $1, $1, 30 addu $2, $1,
  //   $2 sll $0, $0, 0 #nops  sll $0, $0, 0 sll $0, $0, 0  #1b. EX/MEM.RegisterRD == ID/EX.RegisterRt GOOD
  //   addiu $1, $1, 239 addu $2, $2, $1 sll $0, $0, 0 #nops  sll $0, $0, 0 sll $0, $0, 0  #2a.
  //   MEM/WB.RegisterRd == ID/EX.RegisterRs GOOD addiu $1, $1, 2304 addiu $3, $3, 489 #no dependency addu
  //   $2, $1, $2  sll $0, $0, 0 #nops  sll $0, $0, 0 sll $0, $0, 0  #2b. MEM/WB.RegisterRd ==
  //   ID/EX.RegisterRt GOOD addiu $1, $1, -384 addiu $3, $3, 29 #no dependency addu $2, $2, $1  sll $0,
  //   $0, 0 #nops  sll $0, $0, 0 sll $0, $0, 0  #3a. EX/MEM.RegisterRd == ID/EX.RegisterRs AND  #
  //   MEM/WB.RegisterRD == ID/EX.RegisterRt     GOOD addiu $1, $1, 120 addiu $2, $2, -57 addu $3, $1, $2
  //   sll $0, $0, 0 #nops  sll $0, $0, 0 sll $0, $0, 0  #3b. EX/MEM.RegisterRd == ID/EX.RegisterRt AND #
  //   MEM/WB.RegisterRD == ID/EX.RegisterRs     GOOD addiu $1, $1, -239 addiu $2, $2, 6993 addu $3, $2, $1
  //   sll $0, $0, 0 #nops  sll $0, $0, 0 sll $0, $0, 0  #4. EX/MEM.RegisterRd == ID/EX.RegisterRs (insn 2)
  //   #   MEM/WB.RegisterRd == ID/EX.RegisterRs (insn 3)    GOOD addiu $1, $1, 93 subu $1, $1, $2 addu $1,
  //   $1, $3 sll $0, $0, 0 #nops  sll $0, $0, 0 sll $0, $0, 0  #5. EX/MEM.RegisterRd == ID/EX.RegisterRs
  //   (insn 2) #   EX/MEM.RegisterRd == ID/EX.RegisterRs (insn 3)   FAIL!!!! addiu $1, $1, 453 addu $2,
  //   $1, $2 #dep on $1 in EX  addiu $1, $1, 135 #dep on $1 in WB
  //   if/id
  //   id/ex
  //   ex/mem
  //   mem/wb
endmodule

module pc (
  input  clk,
  input  en,
  output [31:0] pc
);

  wire not_1_out;
  wire [31:2] incrementer_1_p2;

  Register #(.width(32)) register_1 (.D({incrementer_1_p2, pc[1:0]}), .en(en), .clk(clk), .Q(pc), .clr(not_1_out));
  not not_1 (not_1_out, en);
  // Incrementer #(.width(30)) incrementer_1: pin names not known; wires that end beside it: pc[31:2], incrementer_1_p2
endmodule

module decode (
  input  [31:0] W,
  input  clk,
  input  wE,
  input  [4:0] rW,
  input  [31:0] Inst,
  output [31:0] A,
  output [31:0] B,
  output [4:0] rd,
  output [4:0] shamt,
  output [11:0] fcn,
  output [31:0] imm,
  output [4:0] rs,
  output [4:0] rt
);

  wire and_1_out, not_1_out;
  wire [5:0] multiplexer_2_out;
  wire [6:6] or_1_out;
  wire [31:0] bit_extender_1_out, bit_extender_2_out, bit_extender_3_out, multiplexer_3_out;

  not not_1 (not_1_out, clk);
  // RegisterFile registerfile_1: pin names not known; wires that end beside it: W, not_1_out, wE, rW, Inst[25:21], Inst[20:16], A, B
  assign bit_extender_1_out = {{27{1'b0}}, Inst[10:6]};  // Bit_Extender bit_extender_1
  Multiplexer #(.width(5), .enable("false")) multiplexer_1 (
    .in0(Inst[15:11]), .in1(Inst[20:16]), .out(rd), .sel(Inst[30]));
  assign bit_extender_2_out = {{16{Inst[15]}}, Inst[15:0]};  // Bit_Extender bit_extender_2
  assign bit_extender_3_out = {{16{1'b0}}, Inst[15:0]};  // Bit_Extender bit_extender_3
  Multiplexer #(.width(6), .enable("false")) multiplexer_2 (
    .in0(Inst[5:0]), .in1(Inst[31:26]), .out(multiplexer_2_out), .sel(or_1_out[6]));
  or or_1 (or_1_out[6], Inst[26], Inst[27], Inst[28], Inst[29], Inst[30], Inst[31]);
  Multiplexer #(.width(32), .enable("false")) multiplexer_3 (
    .in0(bit_extender_2_out), .in1(bit_extender_3_out), .out(multiplexer_3_out), .sel(Inst[29]));
  Multiplexer #(.width(32), .enable("false")) multiplexer_4 (
    .in0(multiplexer_3_out), .in1(bit_extender_1_out), .out(imm), .sel(and_1_out));
  and and_1 (and_1_out, ~or_1_out[6], Inst[3]);  // AND_Gate
  parser parser_1 (
    .ctrl({or_1_out[6], multiplexer_2_out}), .BorI(fcn[4]), .op(fcn[3:0]), .stl(fcn[6]), .lui(fcn[6]),
    .mov(fcn[7]), .\var (fcn[9]), .low(fcn[9]), .jump(fcn[10]), .mem(fcn[11]));

  assign {fcn[8], fcn[5]} = {fcn[9], fcn[6]};
  assign rs = Inst[25:21];
  assign rt = Inst[20:16];
  assign shamt = Inst[10:6];
endmodule

module d_e (
  input  clk,
  input  en,
  input  res,
  input  [31:0] A,
  input  [31:0] B,
  input  [4:0] rd,
  input  [4:0] shamt,
  input  [11:0] fcn,
  input  [31:0] imm,
  input  [4:0] rs,
  input  [4:0] rt,
  output [31:0] out_12,
  output [31:0] out_13,
  output [4:0] out_14,
  output [4:0] out_15,
  output [11:0] out_16,
  output [31:0] out_17,
  output [4:0] out_18,
  output [4:0] out_19
);

  Register #(.width(32)) register_1 (.D(A), .en(en), .clk(clk), .Q(out_12), .clr(res));
  Register #(.width(32)) register_2 (.D(B), .en(en), .clk(clk), .Q(out_13), .clr(res));
  Register #(.width(5)) register_3 (.D(rd), .en(en), .clk(clk), .Q(out_14), .clr(res));
  Register #(.width(5)) register_4 (.D(shamt), .en(en), .clk(clk), .Q(out_15), .clr(res));
  Register #(.width(12)) register_5 (.D(fcn), .en(en), .clk(clk), .Q(out_16), .clr(res));
  Register #(.width(32)) register_6 (.D(imm), .en(en), .clk(clk), .Q(out_17), .clr(res));
  Register #(.width(5)) register_7 (.D(rs), .en(en), .clk(clk), .Q(out_18), .clr(res));
  Register #(.width(5)) register_8 (.D(rt), .en(en), .clk(clk), .Q(out_19), .clr(res));
endmodule

module execute (
  input  [31:0] A,
  input  [31:0] B,
  input  [4:0] rd,
  input  [4:0] shamt,
  input  [11:0] fcn,
  input  [31:0] imm,
  output [31:0] D,
  output [31:0] Bfwd,
  output [4:0] rdo,
  output we
);

  wire comp_1_eq, comp_1_lt, or_1_out, or_2_out;
  wire [4:0] multiplexer_3_out;
  wire [31:0] bit_extender_1_out, bit_extender_2_out, mips_alu_1_p5, multiplexer_1_out, multiplexer_2_out,
       multiplexer_4_out, multiplexer_5_out;

  Multiplexer #(.width(32), .enable("false")) multiplexer_1 (.in0(A), .in1(imm), .out(multiplexer_1_out), .sel(fcn[7]));
  Multiplexer #(.width(32), .enable("false")) multiplexer_2 (.in0(B), .in1(imm), .out(multiplexer_2_out), .sel(fcn[4]));
  Multiplexer #(.width(5), .enable("false")) multiplexer_3 (
    .in0(shamt), .in1(A[4:0]), .out(multiplexer_3_out), .sel(fcn[8]));
  assign bit_extender_1_out = {{16{1'b0}}, imm[15:0]};  // Bit_Extender bit_extender_1
  comp comp_1 (.A(multiplexer_1_out), .B(multiplexer_2_out), .ctrl(fcn[9]), .lt(comp_1_lt), .eq(comp_1_eq));
  // Mips_ALU mips_alu_1: pin names not known; wires that end beside it: A, multiplexer_2_out, fcn[3:0], multiplexer_3_out, mips_alu_1_p5
  assign bit_extender_2_out = {{31{1'b0}}, comp_1_lt};  // Bit_Extender bit_extender_2
  Multiplexer #(.width(32), .enable("false")) multiplexer_4 (
    .in0(mips_alu_1_p5), .in1({bit_extender_1_out[15:0], bit_extender_1_out[31:16]}),
    .out(multiplexer_4_out), .sel(fcn[6]));
  Multiplexer #(.width(32), .enable("false")) multiplexer_5 (
    .in0(bit_extender_2_out), .in1(A), .out(multiplexer_5_out), .sel(fcn[7]));
  Multiplexer #(.width(32), .enable("false")) multiplexer_6 (
    .in0(multiplexer_4_out), .in1(multiplexer_5_out), .out(D), .sel(fcn[5]));
  or or_1 (or_1_out, comp_1_eq, ~fcn[7]);  // OR_Gate
  or or_2 (or_2_out, fcn[10], fcn[11]);
  and and_1 (we, or_1_out, ~or_2_out);  // AND_Gate

  assign Bfwd = {32{1'b0}};
  assign rdo = rd;

  // Notes on the sheet:
  //   16 bit shifter
endmodule

module e_m (
  input  clk,
  input  en,
  input  r,
  input  [31:0] D,
  input  [31:0] B,
  input  [4:0] rd,
  input  we,
  output [31:0] out_8,
  output [31:0] out_9,
  output [4:0] out_10,
  output out_11
);

  Register #(.width(32)) register_1 (.D(D), .en(en), .clk(clk), .Q(out_8), .clr(r));
  Register #(.width(32)) register_2 (.D(B), .en(en), .clk(clk), .Q(out_9), .clr(r));
  Register #(.width(5)) register_3 (.D(rd), .en(en), .clk(clk), .Q(out_10), .clr(r));
  Register #(.width(1)) register_4 (.D(we), .en(en), .clk(clk), .Q(out_11), .clr(r));
endmodule

module memory (
  input  [31:0] D,
  input  [31:0] B,
  input  [4:0] rd,
  input  we,
  output [31:0] Do,
  output [31:0] M,
  output [4:0] rdo,
  output weo
);


  assign Do = D;
  assign M = B;
  assign rdo = rd;
  assign weo = we;
endmodule

module m_w (
  input  clk,
  input  en,
  input  res,
  input  [31:0] D,
  input  [31:0] M,
  input  [4:0] rd,
  input  we,
  output [31:0] out_8,
  output [31:0] out_9,
  output [4:0] out_10,
  output out_11
);

  Register #(.width(32)) register_1 (.D(D), .en(en), .clk(clk), .Q(out_8), .clr(res));
  Register #(.width(32)) register_2 (.D(M), .en(en), .clk(clk), .Q(out_9), .clr(res));
  Register #(.width(5)) register_3 (.D(rd), .en(en), .clk(clk), .Q(out_10), .clr(res));
  Register #(.width(1)) register_4 (.D(we), .en(en), .clk(clk), .Q(out_11), .clr(res));
endmodule

module comp (
  input  [31:0] A,
  input  [31:0] B,
  input  ctrl,
  output lt,
  output eq
);

  wire comparator_1_eq, comparator_1_lt, comparator_2_eq, comparator_2_lt, or_1_out;

  Comparator #(.width(32)) comparator_1 (.a(A), .b(B), .eq(comparator_1_eq), .lt(comparator_1_lt));  // open: gt
  Comparator #(.width(32), .mode("unsigned")) comparator_2 (
    .a(A), .b(B), .eq(comparator_2_eq), .lt(comparator_2_lt));  // open: gt
  Multiplexer #(.enable("false")) multiplexer_1 (.in0(comparator_1_lt), .in1(comparator_2_lt), .out(lt), .sel(ctrl));
  or or_1 (or_1_out, comparator_1_eq, comparator_2_eq);
  xor xor_1 (eq, or_1_out, ctrl);

  // Notes on the sheet:
  //   signed
  //   unsigned
  //   inv
endmodule

module parser (
  input  [6:0] ctrl,
  output BorI,
  output [3:0] op,
  output stl,
  output lui,
  output mov,
  output \var ,
  output low,
  output jump,
  output mem
);

  wire a_out, c_out, v_out, y_out, z_out;
  wire [1:0] f_out;
  wire [3:0] bit_extender_1_out, multiplexer_1_out;

  and a (a_out, ctrl[3], ~ctrl[5]);  // AND_Gate
  and b (f_out[0], ~ctrl[5], ~ctrl[6], ctrl[0]);  // AND_Gate
  and c (c_out, ctrl[1], ~ctrl[2], ctrl[3]);  // AND_Gate
  and d (lui, ctrl[0], ctrl[1], ctrl[2], ctrl[3]);
  and e (\var , ~ctrl[5], ~ctrl[6], ctrl[2]);  // AND_Gate
  and z (z_out, ~ctrl[3], ~ctrl[5], ctrl[6]);  // AND_Gate
  and y (y_out, ~ctrl[1], ctrl[3], ~ctrl[5], ~ctrl[6]);  // AND_Gate
  and x (mem, ctrl[5], ctrl[6]);
  xor f (f_out[1], f_out[0], ctrl[0]);
  and g (mov, c_out, ~ctrl[5], ~ctrl[6]);  // AND_Gate
  or w (jump, z_out, y_out);
  or v (v_out, jump, mem);
  and h (BorI, a_out, ~jump, ~mov);  // AND_Gate
  Multiplexer #(.width(4), .enable("false")) multiplexer_1 (
    .in0({ctrl[2:1], f_out}), .in1({ctrl[3], ctrl[1], ctrl[3], f_out[0]}), .out(multiplexer_1_out),
    .sel(\var ));
  and u (stl, c_out, ~mem);  // AND_Gate
  assign bit_extender_1_out = {{3{v_out}}, v_out};  // Bit_Extender bit_extender_1
  assign op = multiplexer_1_out & ~bit_extender_1_out;  // AND_Gate t, 4 bits wide

  assign low = ctrl[0];
endmodule

module hazard (
  input  emRW,
  input  [4:0] emRD,
  input  [4:0] ieRS,
  input  [4:0] ieRT,
  input  mwRW,
  input  [4:0] mwRD,
  output a,
  output b,
  output ac,
  output bc
);

  wire and_1_out, and_2_out, and_3_out, and_4_out, or_1_out, or_2_out, or_3_out, or_4_out, or_5_out, or_6_out;
  wire [4:0] xor_1_out, xor_2_out, xor_3_out, xor_4_out;

  assign xor_1_out = emRD ^ ieRS;  // XOR_Gate xor_1, 5 bits wide
  assign xor_2_out = emRD ^ ieRT;  // XOR_Gate xor_2, 5 bits wide
  assign xor_3_out = mwRD ^ ieRS;  // XOR_Gate xor_3, 5 bits wide
  assign xor_4_out = mwRD ^ ieRT;  // XOR_Gate xor_4, 5 bits wide
  or or_1 (or_1_out, emRD[0], emRD[1], emRD[2], emRD[3], emRD[4]);
  or or_2 (or_2_out, xor_1_out[0], xor_1_out[1], xor_1_out[2], xor_1_out[3], xor_1_out[4]);
  or or_3 (or_3_out, xor_2_out[0], xor_2_out[1], xor_2_out[2], xor_2_out[3], xor_2_out[4]);
  or or_4 (or_4_out, mwRD[0], mwRD[1], mwRD[2], mwRD[3], mwRD[4]);
  or or_5 (or_5_out, xor_3_out[0], xor_3_out[1], xor_3_out[2], xor_3_out[3], xor_3_out[4]);
  or or_6 (or_6_out, xor_4_out[0], xor_4_out[1], xor_4_out[2], xor_4_out[3], xor_4_out[4]);
  and and_1 (and_1_out, emRW, or_1_out, ~or_2_out);  // AND_Gate
  and and_2 (and_2_out, emRW, or_1_out, ~or_3_out);  // AND_Gate
  and and_3 (and_3_out, mwRW, or_4_out, ~or_5_out);  // AND_Gate
  and and_4 (and_4_out, mwRW, or_4_out, ~or_6_out);  // AND_Gate
  or or_7 (a, and_1_out, and_3_out);
  or or_8 (b, and_2_out, and_4_out);
  and and_5 (ac, ~and_1_out, and_3_out);  // AND_Gate
  and and_6 (bc, ~and_2_out, and_4_out);  // AND_Gate
endmodule
